# Fritzing sketch LoRaWan_Sensor01 (saved by Fritzing 1.0.6)
circuit board: 5.2cm x 3.2cm
breadboards: 1

parts:
  Heltec_CubeCell_Dev-Board1 = Heltec CubeCell Dev-Board [part_number=HTCC-AB01]
  R1 = Resistor [tolerance=±5% power=0.25 resistance=4.7k package=THT]
  R2 = Resistor [tolerance=±5% power=0.25 resistance=4.7k package=THT]
  R3 = Resistor [tolerance=±5% power=0.25 resistance=4.7k package=THT]
  R4 = Resistor [tolerance=±5% power=0.25 resistance=4.7k package=THT]
  R5 = Resistor [tolerance=±5% power=0.25 resistance=4.7k package=THT]
  J1 = female pin header, 2 pins [form="♀ (female)"]
  J2 = female pin header, 2 pins [form="♀ (female)"]
  J3 = female pin header, 3 pins [form="♀ (female)"]
  J4 = female pin header, 2 pins [form="♀ (female)"]
  J5 = female pin header, 2 pins [form="♀ (female)"]
  J6 = female pin header, 2 pins [form="♀ (female)"]
  J7 = female pin header, 3 pins [form="♀ (female)"]

nets:
  N1: Heltec_CubeCell_Dev-Board1.pin2, R2.Pin_0, J6.pin1
  N2: Heltec_CubeCell_Dev-Board1.pin3, R3.Pin_0, J5.pin1
  N3: Heltec_CubeCell_Dev-Board1.pin4, R1.Pin_0, J4.pin1
  N4: Heltec_CubeCell_Dev-Board1.pin_11, Heltec_CubeCell_Dev-Board1.pin_14, Heltec_CubeCell_Dev-Board1.pin_18, J1.pin2, J2.pin2, J3.pin1, J4.pin2, J5.pin2, J6.pin2, J7.pin3
  N5: Heltec_CubeCell_Dev-Board1.pin_13, J2.pin1
  N6: Heltec_CubeCell_Dev-Board1.pin_15, J1.pin1
  N7: Heltec_CubeCell_Dev-Board1.pin_16, R1.Pin_1, R2.Pin_1, R3.Pin_1, R4.Pin_0, R5.Pin_0, J3.pin3, J7.pin1
  N8: Heltec_CubeCell_Dev-Board1.pin_21, R4.Pin_1, J3.pin2
  N9: Heltec_CubeCell_Dev-Board1.pin_22, R5.Pin_1, J7.pin2

notes:
  Send
  Solar
  SW1
  SW2
  SW3
  Temp2
  Temp1
  -  +
  - D +
  + D -
  LoRaWan Sensor01
  Design by: Ch-MG
  V1.0

custom parts:
  Heltec CubeCell Dev-Board: CubeCell is a part of the Heltec LoRa series and incorporates an ASR6501 processor and SX1262 RF transceiver with an integrated CP2102 USB to serial port interface and onboard SHT1.25 battery interface with integrated lithium battery management system supporting direct solar panel connection.
